# Fritzing sketch photocell-to-arduino (saved by Fritzing 0.9.0b)
breadboards: 1

parts:
  Part1 = Arduino Uno (Rev3)
  R1 = Photocell (LDR) [package=THT]
  R2 = Resistor [tolerance=±5% resistance=10k package=THT]

nets:
  N1: Part1.A0, R1.pin_0, R2.Pin_1
  N2: Part1.3V3, R2.Pin_0
  N3: Part1.GND, R1.pin_1
